// Logisim project laberinto.circ as structural Verilog: 5 circuits, main circuit main
module main (
  input  [2:0] H,
  input  [2:0] V,
  input  CLK,
  output [3:0] Izq
);

  wire or_1_out, or_2_out;
  wire [4:0] A_q, multiplexer_1_out, primer_estado_1_a0, sig_estado_1_a2;

  or or_1 (or_1_out, V[0], V[1], V[2], H[0], H[1], H[2]);
  // Probe on A_q
  Primer_Estado primer_estado_1 (
    .H2(H[2]), .H1(H[1]), .H0(H[0]), .V2(V[2]), .V1(V[1]), .V0(V[0]), .E0(primer_estado_1_a0[4]),
    .D0(primer_estado_1_a0[3]), .C0(primer_estado_1_a0[2]), .B0(primer_estado_1_a0[1]),
    .A0(primer_estado_1_a0[0]));
  Sig_Estado sig_estado_1 (
    .E(A_q[4]), .D(A_q[3]), .C(A_q[2]), .B(A_q[1]), .A(A_q[0]), .E2(sig_estado_1_a2[4]),
    .D2(sig_estado_1_a2[3]), .C2(sig_estado_1_a2[2]), .B2(sig_estado_1_a2[1]), .A2(sig_estado_1_a2[0]));
  // Probe on primer_estado_1_a0
  // Probe on sig_estado_1_a2
  Multiplexer #(.width(5), .disabled(0)) multiplexer_1 (
    .in0(primer_estado_1_a0), .in1(sig_estado_1_a2), .out(multiplexer_1_out), .sel(or_2_out), .en(or_1_out));
  // Probe on multiplexer_1_out
  or or_2 (or_2_out, A_q[4], A_q[3], A_q[2], A_q[1], A_q[0]);
  // Probe on multiplexer_1_out
  FF_D E (.D(multiplexer_1_out[4]), .Q(A_q[4]), .CLK(CLK));  // open: nQ
  FF_D D (.D(multiplexer_1_out[3]), .Q(A_q[3]), .CLK(CLK));  // open: nQ
  FF_D C (.D(multiplexer_1_out[2]), .Q(A_q[2]), .CLK(CLK));  // open: nQ
  FF_D B (.D(multiplexer_1_out[1]), .Q(A_q[1]), .CLK(CLK));  // open: nQ
  FF_D A (.D(multiplexer_1_out[0]), .Q(A_q[0]), .CLK(CLK));  // open: nQ
  Logica_Salida logica_salida_1 (
    .E(A_q[4]), .D(A_q[3]), .C(A_q[2]), .B(A_q[1]), .A(A_q[0]), .S3(Izq[3]), .S2(Izq[2]), .S1(Izq[1]),
    .S0(Izq[0]));
  // Probe on A_q

  // Notes on the sheet:
  //   (HORIZ, VERT)
  //   Estado actual
  //   (2) UNA VEZ INICIALIZADOS LOS FLIP FLOPS
  //   SE PUEDEN INGRESAR ENTRADAS
  //   Maximiliano Sepúlveda 201973536-5
  //   Cristopher Fuentes 201973598-5
  //   Estado sig.
  //   Segun coord
  //   Estado sig.
  //   Segun estado
  //   actual
  //   0=Usar coord.
  //   1=Usar estado actual
  //   Mux habilitado
  //   Estado sig.
  //   (1) AL COMENZAR LA SIMULACION
  //   SE DEBE EJECUTAR EL RELOJ AL MENOS UNA VEZ
  //   PARA INICIALIZAR LOS FLIP FLOPS
  //   Estado actual
  //   Arr
  //   Der
  //   Abj
endmodule

module Primer_Estado (
  input  H2,
  input  H1,
  input  H0,
  input  V2,
  input  V1,
  input  V0,
  output E0,
  output D0,
  output C0,
  output B0,
  output A0
);

  wire and_1_out, and_2_out, and_3_out, and_4_out, and_5_out, and_6_out, and_7_out, and_8_out, and_9_out,
       and_10_out, and_11_out, and_12_out, and_13_out, and_14_out, and_15_out, and_16_out, and_17_out,
       and_18_out, and_19_out, and_20_out, and_21_out, and_22_out, and_23_out, and_24_out, and_25_out,
       and_26_out, and_27_out, and_28_out, and_29_out, and_30_out, and_31_out, and_32_out, and_33_out,
       and_34_out, and_35_out, and_36_out, and_37_out, and_38_out, and_39_out, and_40_out, and_41_out,
       and_42_out, and_43_out, and_44_out, and_45_out, and_46_out, not_1_out, not_2_out, not_3_out,
       not_4_out, not_5_out, not_6_out, not_7_out, not_8_out, not_9_out, not_10_out, not_11_out, not_12_out,
       not_13_out, not_14_out, not_15_out, not_16_out, not_17_out, not_18_out, not_19_out, not_20_out,
       not_21_out, not_22_out, not_23_out, not_24_out, not_25_out, not_26_out, not_27_out, not_28_out,
       not_29_out, not_30_out, not_31_out, not_32_out, not_33_out, not_34_out, not_35_out, not_36_out,
       not_37_out, not_38_out, not_39_out, not_40_out, not_41_out, not_42_out, not_43_out, not_44_out,
       not_45_out, not_46_out, not_47_out, not_48_out, not_49_out, not_50_out, not_51_out, not_52_out,
       not_53_out, not_54_out, not_55_out, not_56_out, not_57_out, not_58_out, not_59_out, not_60_out,
       not_61_out, not_62_out, not_63_out, not_64_out, not_65_out, not_66_out, not_67_out, not_68_out,
       not_69_out, not_70_out, not_71_out, not_72_out, not_73_out, not_74_out, not_75_out, not_76_out,
       not_77_out, not_78_out, not_79_out, not_80_out, not_81_out, not_82_out, not_83_out, not_84_out,
       not_85_out, not_86_out;

  not not_1 (not_1_out, H1);
  not not_2 (not_2_out, H0);
  not not_3 (not_3_out, H0);
  not not_4 (not_4_out, V1);
  not not_5 (not_5_out, H1);
  not not_6 (not_6_out, V2);
  not not_7 (not_7_out, V0);
  not not_8 (not_8_out, V2);
  not not_9 (not_9_out, V0);
  not not_10 (not_10_out, V2);
  not not_11 (not_11_out, V1);
  not not_12 (not_12_out, V0);
  not not_13 (not_13_out, H0);
  not not_14 (not_14_out, H2);
  not not_15 (not_15_out, V2);
  not not_16 (not_16_out, V2);
  not not_17 (not_17_out, V1);
  not not_18 (not_18_out, V0);
  not not_19 (not_19_out, H1);
  not not_20 (not_20_out, H0);
  not not_21 (not_21_out, V2);
  not not_22 (not_22_out, H1);
  not not_23 (not_23_out, H0);
  not not_24 (not_24_out, V2);
  not not_25 (not_25_out, H0);
  not not_26 (not_26_out, V1);
  not not_27 (not_27_out, V0);
  not not_28 (not_28_out, H2);
  not not_29 (not_29_out, H0);
  not not_30 (not_30_out, V1);
  not not_31 (not_31_out, H2);
  not not_32 (not_32_out, H0);
  not not_33 (not_33_out, V0);
  not not_34 (not_34_out, H2);
  not not_35 (not_35_out, V0);
  not not_36 (not_36_out, H1);
  not not_37 (not_37_out, H0);
  not not_38 (not_38_out, V2);
  not not_39 (not_39_out, V2);
  not not_40 (not_40_out, V0);
  not not_41 (not_41_out, H1);
  not not_42 (not_42_out, V0);
  not not_43 (not_43_out, H2);
  not not_44 (not_44_out, H1);
  not not_45 (not_45_out, V2);
  not not_46 (not_46_out, V0);
  not not_47 (not_47_out, H1);
  not not_48 (not_48_out, H2);
  not not_49 (not_49_out, H0);
  not not_50 (not_50_out, V1);
  not not_51 (not_51_out, H2);
  not not_52 (not_52_out, H0);
  not not_53 (not_53_out, V0);
  not not_54 (not_54_out, H2);
  not not_55 (not_55_out, V2);
  not not_56 (not_56_out, H2);
  not not_57 (not_57_out, V1);
  not not_58 (not_58_out, V0);
  not not_59 (not_59_out, H1);
  not not_60 (not_60_out, H0);
  not not_61 (not_61_out, H0);
  not not_62 (not_62_out, V2);
  not not_63 (not_63_out, V0);
  not not_64 (not_64_out, V2);
  not not_65 (not_65_out, V1);
  not not_66 (not_66_out, H2);
  not not_67 (not_67_out, V2);
  not not_68 (not_68_out, V1);
  not not_69 (not_69_out, H2);
  not not_70 (not_70_out, H1);
  not not_71 (not_71_out, H2);
  not not_72 (not_72_out, H0);
  not not_73 (not_73_out, V0);
  not not_74 (not_74_out, V2);
  not not_75 (not_75_out, V1);
  not not_76 (not_76_out, V1);
  not not_77 (not_77_out, V0);
  not not_78 (not_78_out, H1);
  not not_79 (not_79_out, H0);
  not not_80 (not_80_out, H1);
  not not_81 (not_81_out, V1);
  not not_82 (not_82_out, H0);
  not not_83 (not_83_out, V1);
  not not_84 (not_84_out, H0);
  not not_85 (not_85_out, V2);
  not not_86 (not_86_out, V0);
  and and_1 (and_1_out, H2, not_1_out, not_2_out, V2);
  and and_2 (and_2_out, H2, not_3_out, V2, not_4_out);
  and and_3 (and_3_out, H2, not_5_out, V2, V0);
  and and_4 (and_4_out, H2, V2, V1, V0);
  and and_5 (and_5_out, H2, H0, not_6_out, V1, not_7_out);
  and and_6 (and_6_out, H2, H1, not_8_out, V1, not_9_out);
  and and_7 (and_7_out, H2, H1, H0, not_10_out, not_11_out, V0);
  and and_8 (and_8_out, H2, H1, H0, V2, not_12_out);
  and and_9 (and_9_out, H1, not_13_out, V2, V1, V0);
  and and_10 (and_10_out, not_14_out, H1, H0, not_15_out, V0);
  and and_11 (and_11_out, H1, H0, not_16_out, not_17_out, V0);
  and and_12 (and_12_out, H1, H0, V2, not_18_out);
  and and_13 (and_13_out, H2, not_19_out, not_20_out, not_21_out, V0);
  and and_14 (and_14_out, H2, not_22_out, not_23_out, not_24_out, V1);
  and and_15 (and_15_out, H2, H1, not_25_out, V2, not_26_out);
  and and_16 (and_16_out, H2, H1, H0, V1, not_27_out);
  and and_17 (and_17_out, H2, H1, H0, V2, V1);
  and and_18 (and_18_out, not_28_out, H1, not_29_out, not_30_out, V0);
  and and_19 (and_19_out, not_31_out, H1, not_32_out, V2, not_33_out);
  and and_20 (and_20_out, not_34_out, H1, V2, V1, not_35_out);
  and and_21 (and_21_out, H2, not_36_out, not_37_out, not_38_out, V0);
  and and_22 (and_22_out, H2, not_39_out, V1, not_40_out);
  and and_23 (and_23_out, H2, not_41_out, H0, V2, V0);
  and and_24 (and_24_out, H2, H1, H0, V2, not_42_out);
  and and_25 (and_25_out, H2, H1, H0, V2, V1);
  and and_26 (and_26_out, not_43_out, not_44_out, H0, not_45_out, V1, not_46_out);
  and and_27 (and_27_out, not_47_out, H0, V2, V1, V0);
  and and_28 (and_28_out, not_48_out, H1, not_49_out, V2, not_50_out, V0);
  and and_29 (and_29_out, not_51_out, H1, not_52_out, V2, V1, not_53_out);
  and and_30 (and_30_out, not_54_out, H1, H0, not_55_out, V1, V0);
  and and_31 (and_31_out, not_56_out, H1, H0, V2, not_57_out, not_58_out);
  and and_32 (and_32_out, H2, not_59_out, not_60_out, V1);
  and and_33 (and_33_out, H2, not_61_out, not_62_out, V1, not_63_out);
  and and_34 (and_34_out, H2, V2, V1, V0);
  and and_35 (and_35_out, H2, H1, H0, not_64_out, not_65_out, V0);
  and and_36 (and_36_out, H2, H1, H0, V2, V1);
  and and_37 (and_37_out, not_66_out, H0, not_67_out, not_68_out, V0);
  and and_38 (and_38_out, not_69_out, not_70_out, H0, V2, V1, V0);
  and and_39 (and_39_out, not_71_out, H1, not_72_out, V2, not_73_out);
  and and_40 (and_40_out, H1, H0, not_74_out, not_75_out, V0);
  and and_41 (and_41_out, H1, H0, V2, not_76_out, not_77_out);
  and and_42 (and_42_out, H2, not_78_out, not_79_out, V0);
  and and_43 (and_43_out, H2, not_80_out, V2, not_81_out, V0);
  and and_44 (and_44_out, H2, not_82_out, V2, not_83_out, V0);
  and and_45 (and_45_out, H2, H1, not_84_out, not_85_out, V1, not_86_out);
  and and_46 (and_46_out, H2, H1, H0, V2, V1, V0);
  or or_1 (E0, and_1_out, and_2_out, and_3_out, and_4_out, and_5_out, and_6_out, and_7_out, and_8_out);
  or or_2 (D0, and_9_out, and_10_out, and_11_out, and_12_out, and_13_out, and_14_out, and_15_out, and_16_out, and_17_out);
  or or_3 (C0, and_18_out, and_19_out, and_20_out, and_21_out, and_22_out, and_23_out, and_24_out, and_25_out);
  or or_4 (B0, and_26_out, and_27_out, and_28_out, and_29_out, and_30_out, and_31_out, and_32_out, and_33_out, and_34_out, and_35_out, and_36_out);
  or or_5 (A0, and_37_out, and_38_out, and_39_out, and_40_out, and_41_out, and_42_out, and_43_out, and_44_out, and_45_out, and_46_out);
endmodule

module Sig_Estado (
  input  E,
  input  D,
  input  C,
  input  B,
  input  A,
  output E2,
  output D2,
  output C2,
  output B2,
  output A2
);

  wire and_1_out, and_2_out, and_3_out, and_4_out, and_5_out, and_6_out, and_7_out, and_8_out, and_9_out,
       and_10_out, and_11_out, and_12_out, and_13_out, and_14_out, and_15_out, and_16_out, and_17_out,
       and_18_out, and_19_out, and_20_out, and_21_out, and_22_out, and_23_out, and_24_out, and_25_out,
       and_26_out, and_27_out, and_28_out, and_29_out, and_30_out, and_31_out, and_32_out, and_33_out,
       and_34_out, not_1_out, not_2_out, not_3_out, not_4_out, not_5_out, not_6_out, not_7_out, not_8_out,
       not_9_out, not_10_out, not_11_out, not_12_out, not_13_out, not_14_out, not_15_out, not_16_out,
       not_17_out, not_18_out, not_19_out, not_20_out, not_21_out, not_22_out, not_23_out, not_24_out,
       not_25_out, not_26_out, not_27_out, not_28_out, not_29_out, not_30_out, not_31_out, not_32_out,
       not_33_out, not_34_out, not_35_out, not_36_out, not_37_out, not_38_out, not_39_out, not_40_out,
       not_41_out, not_42_out, not_43_out, not_44_out, not_45_out, not_46_out, not_47_out, not_48_out,
       not_49_out, not_50_out, not_51_out, not_52_out;

  not not_1 (not_1_out, C);
  not not_2 (not_2_out, B);
  not not_3 (not_3_out, A);
  not not_4 (not_4_out, C);
  not not_5 (not_5_out, E);
  not not_6 (not_6_out, D);
  not not_7 (not_7_out, D);
  not not_8 (not_8_out, B);
  not not_9 (not_9_out, B);
  not not_10 (not_10_out, E);
  not not_11 (not_11_out, A);
  not not_12 (not_12_out, C);
  not not_13 (not_13_out, B);
  not not_14 (not_14_out, D);
  not not_15 (not_15_out, C);
  not not_16 (not_16_out, B);
  not not_17 (not_17_out, E);
  not not_18 (not_18_out, A);
  not not_19 (not_19_out, D);
  not not_20 (not_20_out, E);
  not not_21 (not_21_out, C);
  not not_22 (not_22_out, B);
  not not_23 (not_23_out, B);
  not not_24 (not_24_out, B);
  not not_25 (not_25_out, A);
  not not_26 (not_26_out, A);
  not not_27 (not_27_out, C);
  not not_28 (not_28_out, E);
  not not_29 (not_29_out, B);
  not not_30 (not_30_out, E);
  not not_31 (not_31_out, A);
  not not_32 (not_32_out, A);
  not not_33 (not_33_out, D);
  not not_34 (not_34_out, C);
  not not_35 (not_35_out, A);
  not not_36 (not_36_out, E);
  not not_37 (not_37_out, A);
  not not_38 (not_38_out, D);
  not not_39 (not_39_out, A);
  not not_40 (not_40_out, E);
  not not_41 (not_41_out, D);
  not not_42 (not_42_out, B);
  not not_43 (not_43_out, A);
  not not_44 (not_44_out, E);
  not not_45 (not_45_out, C);
  not not_46 (not_46_out, B);
  not not_47 (not_47_out, D);
  not not_48 (not_48_out, C);
  not not_49 (not_49_out, B);
  not not_50 (not_50_out, B);
  not not_51 (not_51_out, B);
  not not_52 (not_52_out, A);
  and and_1 (and_1_out, D, not_1_out, B, A);
  and and_2 (and_2_out, D, C, not_2_out, not_3_out);
  and and_3 (and_3_out, E, not_4_out);
  and and_4 (and_4_out, E, A);
  and and_5 (and_5_out, E, B);
  and and_6 (and_6_out, not_5_out, not_6_out, B, A);
  and and_7 (and_7_out, not_7_out, C, not_8_out);
  and and_8 (and_8_out, D, not_9_out, A);
  and and_9 (and_9_out, not_10_out, D, B, not_11_out);
  and and_10 (and_10_out, D, C, B);
  and and_11 (and_11_out, E, D, not_12_out, not_13_out);
  and and_12 (and_12_out, E, D, A);
  and and_13 (and_13_out, not_14_out, not_15_out, not_16_out, A);
  and and_14 (and_14_out, not_17_out, C, B, not_18_out);
  and and_15 (and_15_out, not_19_out, C, B, A);
  and and_16 (and_16_out, not_20_out, D, not_21_out, not_22_out);
  and and_17 (and_17_out, D, C, not_23_out, A);
  and and_18 (and_18_out, E, C, not_24_out, not_25_out);
  and and_19 (and_19_out, E, D, not_26_out);
  and and_20 (and_20_out, E, D, not_27_out, B);
  and and_21 (and_21_out, not_28_out, C, not_29_out, A);
  and and_22 (and_22_out, not_30_out, D, not_31_out);
  and and_23 (and_23_out, D, B, not_32_out);
  and and_24 (and_24_out, D, C, B);
  and and_25 (and_25_out, E, not_33_out, not_34_out, B, A);
  and and_26 (and_26_out, E, C, not_35_out);
  and and_27 (and_27_out, not_36_out, B, not_37_out);
  and and_28 (and_28_out, not_38_out, B, not_39_out);
  and and_29 (and_29_out, not_40_out, not_41_out, C, not_42_out);
  and and_30 (and_30_out, C, B, not_43_out);
  and and_31 (and_31_out, not_44_out, D, not_45_out, not_46_out);
  and and_32 (and_32_out, E, not_47_out, not_48_out, not_49_out);
  and and_33 (and_33_out, E, C, not_50_out, A);
  and and_34 (and_34_out, E, D, not_51_out, not_52_out);
  or or_1 (E2, and_1_out, and_2_out, and_3_out, and_4_out, and_5_out);
  or or_2 (D2, and_6_out, and_7_out, and_8_out, and_9_out, and_10_out, and_11_out, and_12_out);
  or or_3 (C2, and_13_out, and_14_out, and_15_out, and_16_out, and_17_out, and_18_out, and_19_out, and_20_out);
  or or_4 (B2, and_21_out, and_22_out, and_23_out, and_24_out, and_25_out, and_26_out);
  or or_5 (A2, and_27_out, and_28_out, and_29_out, and_30_out, and_31_out, and_32_out, and_33_out, and_34_out);
endmodule

module Logica_Salida (
  input  E,
  input  D,
  input  C,
  input  B,
  input  A,
  output S3,
  output S2,
  output S1,
  output S0
);

  wire and_1_out, and_2_out, and_3_out, and_4_out, and_5_out, and_6_out, and_7_out, and_8_out, and_9_out,
       and_10_out, and_11_out, and_12_out, and_13_out, and_14_out, and_15_out, and_16_out, and_17_out,
       and_18_out, and_19_out, and_20_out, not_1_out, not_2_out, not_3_out, not_4_out, not_5_out, not_6_out,
       not_7_out, not_8_out, not_9_out, not_10_out, not_11_out, not_12_out, not_13_out, not_14_out,
       not_15_out, not_16_out, not_17_out, not_18_out, not_19_out, not_20_out, not_21_out, not_22_out,
       not_23_out, not_24_out, not_25_out, not_26_out, not_27_out, not_28_out, not_29_out, not_30_out,
       not_31_out, not_32_out, not_33_out, not_34_out, not_35_out, not_36_out, not_37_out, not_38_out;

  not not_1 (not_1_out, D);
  not not_2 (not_2_out, A);
  not not_3 (not_3_out, D);
  not not_4 (not_4_out, C);
  not not_5 (not_5_out, A);
  not not_6 (not_6_out, B);
  not not_7 (not_7_out, E);
  not not_8 (not_8_out, D);
  not not_9 (not_9_out, A);
  not not_10 (not_10_out, E);
  not not_11 (not_11_out, C);
  not not_12 (not_12_out, B);
  not not_13 (not_13_out, A);
  not not_14 (not_14_out, D);
  not not_15 (not_15_out, C);
  not not_16 (not_16_out, B);
  not not_17 (not_17_out, E);
  not not_18 (not_18_out, A);
  not not_19 (not_19_out, B);
  not not_20 (not_20_out, A);
  not not_21 (not_21_out, D);
  not not_22 (not_22_out, C);
  not not_23 (not_23_out, B);
  not not_24 (not_24_out, A);
  not not_25 (not_25_out, C);
  not not_26 (not_26_out, E);
  not not_27 (not_27_out, D);
  not not_28 (not_28_out, E);
  not not_29 (not_29_out, C);
  not not_30 (not_30_out, D);
  not not_31 (not_31_out, B);
  not not_32 (not_32_out, E);
  not not_33 (not_33_out, B);
  not not_34 (not_34_out, A);
  not not_35 (not_35_out, B);
  not not_36 (not_36_out, C);
  not not_37 (not_37_out, B);
  not not_38 (not_38_out, A);
  and and_1 (and_1_out, D, C, B, A);
  and and_2 (and_2_out, E, not_1_out, C, not_2_out);
  and and_3 (and_3_out, E, not_3_out, C, B);
  and and_4 (and_4_out, E, D, not_4_out, B, not_5_out);
  and and_5 (and_5_out, E, D, C, not_6_out);
  and and_6 (and_6_out, not_7_out, not_8_out, B, not_9_out);
  and and_7 (and_7_out, not_10_out, D, not_11_out, not_12_out, not_13_out);
  and and_8 (and_8_out, E, not_14_out, not_15_out, B);
  and and_9 (and_9_out, E, D, not_16_out, A);
  and and_10 (and_10_out, not_17_out, D, B, not_18_out);
  and and_11 (and_11_out, D, C, not_19_out, A);
  and and_12 (and_12_out, D, C, B, not_20_out);
  and and_13 (and_13_out, E, not_21_out, not_22_out, not_23_out, not_24_out);
  and and_14 (and_14_out, E, D, not_25_out, B, A);
  and and_15 (and_15_out, not_26_out, not_27_out, A);
  and and_16 (and_16_out, not_28_out, not_29_out, A);
  and and_17 (and_17_out, not_30_out, not_31_out, A);
  and and_18 (and_18_out, not_32_out, C, not_33_out, not_34_out);
  and and_19 (and_19_out, E, C, not_35_out, A);
  and and_20 (and_20_out, E, D, not_36_out, not_37_out, not_38_out);
  or or_1 (S3, and_1_out, and_2_out, and_3_out, and_4_out, and_5_out);
  or or_2 (S2, and_6_out, and_7_out, and_8_out, and_9_out);
  or or_3 (S1, and_10_out, and_11_out, and_12_out, and_13_out, and_14_out);
  or or_4 (S0, and_15_out, and_16_out, and_17_out, and_18_out, and_19_out, and_20_out);
endmodule

module FF_D (
  input  CLK,
  input  D,
  output Q,
  output nQ
);

  wire and_1_out, and_2_out, and_3_out, and_4_out, buffer_1_out, buffer_2_out, nor_1_out, nor_2_out,
       not_1_out, not_2_out;

  buf buffer_1 (buffer_1_out, D);
  not not_1 (not_1_out, D);
  not not_2 (not_2_out, CLK);
  and and_1 (and_1_out, not_2_out, buffer_1_out);
  and and_2 (and_2_out, not_1_out, not_2_out);
  nor nor_1 (nor_1_out, and_1_out, nor_2_out);
  nor nor_2 (nor_2_out, nor_1_out, and_2_out);
  buf buffer_2 (buffer_2_out, nor_2_out);
  and and_3 (and_3_out, CLK, nor_1_out);
  and and_4 (and_4_out, buffer_2_out, CLK);
  nor nor_3 (Q, and_3_out, nQ);
  nor nor_4 (nQ, Q, and_4_out);

  // Notes on the sheet:
  //   CLK: pull=up
  //   Master
  //   El reloj debe pasar a 1 al menos una vez para
  //   inicializar las salidas
  //   Slave
endmodule
