// Logisim project Ayudantia 5-2.circ as structural Verilog: 4 circuits, main circuit main
module main (
  input  X,
  output out_2
);

  wire and_1_out, and_2_out, and_3_out, and_4_out, and_5_out, and_6_out, button_1_out, not_1_out, or_1_out,
       S0_nq, S0_q, S1_q, S2_q;

  not not_1 (not_1_out, X);
  and and_1 (and_1_out, S0_q, not_1_out);
  and and_2 (and_2_out, X, S2_q);
  and and_3 (and_3_out, S0_nq, S1_q, X);
  and and_4 (and_4_out, S0_nq, not_1_out);
  or or_1 (or_1_out, and_1_out, and_2_out, and_3_out);
  LED led_1 (.in(and_4_out));
  LED led_2 (.in(X));
  LED led_3 (.in(or_1_out));
  Button button_1 (.out(button_1_out));
  FF_D S0 (.D(X), .CLK(button_1_out), .Q(S0_q), .nQ(S0_nq));
  FF_D S1 (.D(or_1_out), .CLK(button_1_out), .Q(S1_q));  // open: nQ
  FF_D S2 (.D(and_4_out), .CLK(button_1_out), .Q(S2_q));  // open: nQ
  LED led_4 (.in(S0_q));
  LED led_5 (.in(S2_q));
  LED led_6 (.in(S1_q));
  and and_5 (and_5_out, S1_q, S0_q, not_1_out);
  and and_6 (and_6_out, S1_q, S0_nq, X);
  or or_2 (out_2, and_5_out, and_6_out);

  // Notes on the sheet:
  //   Siguiente Estado
  //   Estado Actual
endmodule

module FF_D (
  input  CLK,
  input  D,
  output Q,
  output nQ
);

  wire latchd_1_q, not_1_out;

  LatchD latchd_1 (.Q(latchd_1_q), .D(D), .CLK(not_1_out));  // open: nQ
  not not_1 (not_1_out, CLK);
  LatchD latchd_2 (.nQ(nQ), .Q(Q), .D(latchd_1_q), .CLK(CLK));
endmodule

module LatchD (
  input  CLK,
  input  D,
  output Q,
  output nQ
);

  wire and_1_out, and_2_out, not_1_out;

  not not_1 (not_1_out, D);
  and and_1 (and_1_out, CLK, not_1_out);
  and and_2 (and_2_out, CLK, D);
  nor nor_1 (Q, and_1_out, nQ);
  nor nor_2 (nQ, Q, and_2_out);
endmodule

module Circuito_Logico (
  input  Z,
  input  Y,
  input  X,
  output U,
  output T,
  output F,
  output S,
  output M
);

  wire and_1_out, and_2_out, and_3_out, and_4_out, and_5_out, not_1_out, not_2_out, not_3_out, not_4_out;

  not not_1 (not_1_out, Y);
  not not_2 (not_2_out, X);
  and and_1 (and_1_out, Y, X);
  not not_3 (not_3_out, X);
  not not_4 (not_4_out, Y);
  and and_2 (and_2_out, not_1_out, X);
  and and_3 (and_3_out, Y, not_2_out);
  or or_1 (F, and_1_out, Z);
  and and_4 (and_4_out, Y, not_3_out);
  and and_5 (and_5_out, not_4_out, X);
  or or_2 (U, and_2_out, Z);
  or or_3 (T, and_3_out, Z);
  or or_4 (S, and_4_out, Z);
  or or_5 (M, and_5_out, Z);
endmodule
