// Logisim project Ejemplo.circ as structural Verilog: 3 circuits, main circuit main
module main (
  input  X,
  output out_2
);

  wire A_nq, A_q, and_1_out, and_2_out, B_nq, B_q, clock_1_out, or_1_out;

  or or_1 (or_1_out, B_q, A_q);
  and and_1 (and_1_out, X, or_1_out);
  and and_2 (and_2_out, X, A_nq, B_nq);
  Clock clock_1 (.out(clock_1_out));
  FF_D A (.D(and_2_out), .CLK(clock_1_out), .Q(A_q), .nQ(A_nq));
  FF_D B (.D(and_1_out), .CLK(clock_1_out), .Q(B_q), .nQ(B_nq));
  and and_3 (out_2, X, A_nq, B_q);
endmodule

module FF_D (
  input  CLK,
  input  D,
  output Q,
  output nQ
);

  wire latchd_1_q, not_1_out;

  LatchD latchd_1 (.Q(latchd_1_q), .D(D), .CLK(not_1_out));  // open: nQ
  not not_1 (not_1_out, CLK);
  LatchD latchd_2 (.nQ(nQ), .Q(Q), .D(latchd_1_q), .CLK(CLK));
endmodule

module LatchD (
  input  CLK,
  input  D,
  output Q,
  output nQ
);

  wire and_1_out, and_2_out, not_1_out;

  not not_1 (not_1_out, D);
  and and_1 (and_1_out, CLK, not_1_out);
  and and_2 (and_2_out, CLK, D);
  nor nor_1 (Q, and_1_out, nQ);
  nor nor_2 (nQ, Q, and_2_out);
endmodule
