// Logisim project UTFSM.circ as structural Verilog: 2 circuits, main circuit main
module main (
  input  in_1
);

  wire A_q, A_qn, and_1_out, and_2_out, and_3_out, and_4_out, and_5_out, and_6_out, and_7_out, and_8_out,
       and_9_out, and_10_out, B_q, B_qn, button_1_out, C_q, C_qn, letras_1_f_2, letras_1_m, letras_1_s,
       letras_1_t_2, letras_1_u_2, not_1_out, or_1_out, or_2_out, or_3_out, or_4_out, or_5_out, or_6_out;

  not not_1 (not_1_out, in_1);
  and and_1 (and_1_out, in_1, C_qn, A_qn);
  and and_2 (and_2_out, not_1_out, A_q);
  and and_3 (and_3_out, not_1_out, B_q);
  and and_4 (and_4_out, in_1, B_qn, A_q);
  and and_5 (and_5_out, B_q, A_qn);
  and and_6 (and_6_out, not_1_out, C_q);
  and and_7 (and_7_out, in_1, B_q, A_q);
  or or_1 (or_1_out, and_1_out, and_2_out);
  or or_2 (or_2_out, and_3_out, and_4_out, and_5_out);
  or or_3 (or_3_out, and_6_out, and_7_out);
  Button button_1 (.out(button_1_out));
  D_Flip_Flop A (.clk(button_1_out), .D(or_1_out), .Q(A_q), .Qn(A_qn));  // open: preset, en, reset
  D_Flip_Flop B (.clk(button_1_out), .D(or_2_out), .Q(B_q), .Qn(B_qn));  // open: preset, en, reset
  D_Flip_Flop C (.clk(button_1_out), .D(or_3_out), .Q(C_q), .Qn(C_qn));  // open: preset, en, reset
  or or_4 (or_4_out, C_q, and_8_out);
  and and_8 (and_8_out, B_qn, A_q);
  or or_5 (or_5_out, C_q, and_9_out);
  and and_9 (and_9_out, B_q, A_qn);
  or or_6 (or_6_out, C_q, and_10_out);
  and and_10 (and_10_out, B_q, A_q);
  LED U (.in(letras_1_u_2));
  Letras letras_1 (
    .U(or_4_out), .T(or_5_out), .F(or_6_out), .U_2(letras_1_u_2), .T_2(letras_1_t_2), .F_2(letras_1_f_2),
    .S(letras_1_s), .M(letras_1_m));
  LED T (.in(letras_1_t_2));
  LED M (.in(letras_1_m));
  LED S (.in(letras_1_s));
  LED F (.in(letras_1_f_2));

  // Notes on the sheet:
  //   -X        X
  //   -C    C
  //   -B    B
  //   -A    A
  //   -C    C
  //   -B    B
  //   -A    A
endmodule

module Letras (
  input  U,
  input  T,
  input  F,
  output U_2,
  output T_2,
  output F_2,
  output S,
  output M
);


  assign F_2 = F;
  assign M = U;
  assign S = T;
  assign T_2 = T;
  assign U_2 = U;
endmodule
